# Fritzing sketch RF-Receiver-Basic (saved by Fritzing 0.9.2b)
breadboards: 1

parts:
  Parte1 = Arduino Uno (Rev3) - ICSP
  U1 = RF-LINK_RX [package=rf-link_rx]

nets:
  5V: Parte1.5V, U1.+5V
  GND: Parte1.GND, U1.GND
  N1: Parte1.D11_PWM/MOSI, U1.DATA
