# Fritzing sketch RF-Receiver-LCD (saved by Fritzing 0.9.2b)
breadboards: 1

parts:
  Parte1 = Arduino Uno (Rev3) - ICSP
  U1 = RF-LINK_RX [package=rf-link_rx]
  R1 = TRIMPOT [package=trimpot_pth_s3_lock]
  U2 = LCD-16X2 [package=lcd-16x2]

nets:
  N1: Parte1.D11_PWM/MOSI, U1.DATA
  N2: Parte1.D2, U2.DB7
  N3: Parte1.D3_PWM, U2.DB6
  N4: Parte1.D4, U2.DB5
  N5: Parte1.D5_PWM, U2.DB4
  N6: Parte1.D6_PWM, U2.E
  N7: Parte1.D7, U2.RS
  5V: Parte1.5V, U1.+5V, R1.CCW, U2.VDD, U2.A
  GND: Parte1.GND, U1.GND, R1.CW, U2.VSS, U2.R_W, U2.K
  N8: R1.WIPER, U2.VO
